// Logisim project logisim74.circ as structural Verilog: 16 circuits, main circuit main
module main (
  input  [15:0] PC,
  input  [15:0] MR,
  input  [7:0] in_3,
  input  [7:0] in_4,
  input  [7:0] in_5,
  input  [7:0] in_6,
  input  [1:0] Update_IR,
  input  [3:0] ALU
);

  wire ALU_garry, ALU_zero, button_1_out, clock_1_out, CU_increment_p, CU_ram_select_m, CU_reset_p1,
       CU_update_ramsosse, dip_74138_1_p4, dip_74138_1_p6, dip_74138_1_p8, dip_74138_1_p9, dip_74138_1_p10,
       dip_74138_1_p11, dip_74138_1_p12, dip_74138_1_p13;
  wire [2:0] CU_bus_input, CU_update_reg;
  wire [7:0] undriven_2;
  wire [15:0] undriven;

  Clock clock_1 (.out(clock_1_out));
  Button button_1 (.out(button_1_out));
  RAM #(.addrWidth(16)) ram_1 (.addr(undriven));  // open: data, sel, clk, ld, clr
  PC74 u_PC (
    .P2(dip_74138_1_p12), .BUS_in(undriven_2), .Reset_P1(CU_reset_p1), .P1(dip_74138_1_p13), .Bus_out(PC),
    .Clock(CU_increment_p));
  ControlUnit74 CU (
    .Clock(clock_1_out), .Reset(button_1_out), .Bus_in(undriven_2), .Carry(ALU_zero), .isZero(ALU_garry),
    .Increment_P(CU_increment_p), .Bus_Input(CU_bus_input), .Update_Reg(CU_update_reg),
    .Reset_P1(CU_reset_p1), .Alu(ALU), .Update_RAMSOSSE(CU_update_ramsosse), .RAM_select_M(CU_ram_select_m),
    .Update_IR(Update_IR));  // open: in_4
  // DIP_74138 dip_74138_1: pin names not known; wires that end beside it: CU_update_ramsosse, CU_ram_select_m, CU_update_reg[2], dip_74138_1_p4, CU_update_reg[1], dip_74138_1_p6, CU_update_reg[0], dip_74138_1_p8, dip_74138_1_p9, dip_74138_1_p10, dip_74138_1_p11, dip_74138_1_p12, dip_74138_1_p13
  REGISTER74 M2 (.Set(dip_74138_1_p11), .Output(MR[7:0]));  // open: Input
  REGISTER74 M1 (.Set(dip_74138_1_p10), .Output(MR[15:8]));  // open: Input
  // DIP_74138 dip_74138_2: pin names not known; wires that end beside it: CU_bus_input[2], CU_bus_input[1], CU_bus_input[0]
  REGISTER74 C (.Input(undriven_2), .Set(dip_74138_1_p9), .Output(in_3));
  REGISTER74 D (.Input(undriven_2), .Set(dip_74138_1_p8), .Output(in_4));
  REGISTER74 A (.Input(undriven_2), .Set(dip_74138_1_p4), .Output(in_5));
  REGISTER74 B (.Input(undriven_2), .Set(dip_74138_1_p6), .Output(in_6));
  ALU74 u_ALU (.A(in_5), .B(in_6), .CU(ALU), .Zero(ALU_zero), .Garry(ALU_garry));  // open: Bus
  // DIP_7474 Zero_Carry: pin names not known; wires that end beside it: clock_1_out, clock_1_out, ALU_garry, ALU_zero
endmodule

module PC74 (
  input  P2,
  input  [7:0] BUS_in,
  input  Reset_P1,
  input  Clock,
  input  P1,
  output [15:0] Bus_out
);

  wire AND_p3, dip_7404_1_p3, dip_7404_1_p4, dip_7404_1_p5, dip_7404_1_p6, OR_p3;
  wire [7:0] AND_2_p3, buffer_1_out, buffer_2_out, D_FF_2_p2, MUX_p4, XOR_p6;
  wire [7:1] XOR_p8;

  // DIP_7408 AND: pin names not known; wires that end beside it: P2, Clock, AND_p3
  // DIP_7404 dip_7404_1: pin names not known; wires that end beside it: Reset_P1, AND_p3, dip_7404_1_p3, dip_7404_1_p4, dip_7404_1_p5, dip_7404_1_p6
  // DIP_7432 OR: pin names not known; wires that end beside it: Reset_P1, P1, OR_p3, OR_p3, Clock, dip_7404_1_p5
  // DIP_7486 XOR: pin names not known; wires that end beside it: Bus_out[7], Clock, XOR_p8[7], Bus_out[0], XOR_p6[7], XOR_p6[0], Bus_out[6], XOR_p8[1], XOR_p8[6], Bus_out[1], XOR_p6[6], XOR_p6[1]
  // DIP_7474 D_FF: pin names not known; wires that end beside it: 1'b1, BUS_in[0], dip_7404_1_p4, 1'b1, Bus_out[8], 1'b1, 1'b1, BUS_in[1], dip_7404_1_p4, Bus_out[9]
  // DIP_7408 AND_2: pin names not known; wires that end beside it: BUS_in[0], dip_7404_1_p3, AND_2_p3[0], BUS_in[1], dip_7404_1_p3, AND_2_p3[1], BUS_in[3], dip_7404_1_p3, AND_2_p3[3], BUS_in[2], dip_7404_1_p3, AND_2_p3[2]
  // DIP_7474 D_FF_2: pin names not known; wires that end beside it: 1'b1, D_FF_2_p2[0], dip_7404_1_p6, 1'b1, Bus_out[0], 1'b1, 1'b1, D_FF_2_p2[1], dip_7404_1_p6, Bus_out[1]
  // DIP_7486 XOR_2: pin names not known; wires that end beside it: Bus_out[5], XOR_p8[2], XOR_p8[5], Bus_out[2], XOR_p6[5], XOR_p6[2], Bus_out[4], XOR_p8[3], XOR_p8[4], Bus_out[3], XOR_p6[4], XOR_p6[3]
  // DIP_7408 AND_3: pin names not known; wires that end beside it: Bus_out[7], Bus_out[0], XOR_p8[7], Clock, XOR_p8[1], Bus_out[6], Bus_out[1], XOR_p8[6], XOR_p8[1], XOR_p8[7], XOR_p8[2]
  // DIP_7474 D_FF_3: pin names not known; wires that end beside it: 1'b1, D_FF_2_p2[2], dip_7404_1_p6, 1'b1, Bus_out[2], 1'b1, D_FF_2_p2[3], dip_7404_1_p6, Bus_out[3]
  // DIP_7474 D_FF_4: pin names not known; wires that end beside it: 1'b1, BUS_in[2], dip_7404_1_p4, 1'b1, Bus_out[10], 1'b1, 1'b1, BUS_in[3], dip_7404_1_p4, Bus_out[11]
  // DIP_7408 AND_4: pin names not known; wires that end beside it: BUS_in[4], dip_7404_1_p3, AND_2_p3[4], BUS_in[5], dip_7404_1_p3, AND_2_p3[5], BUS_in[7], dip_7404_1_p3, AND_2_p3[7], BUS_in[6], dip_7404_1_p3, AND_2_p3[6]
  // DIP_7474 D_FF_5: pin names not known; wires that end beside it: 1'b1, BUS_in[4], dip_7404_1_p4, 1'b1, Bus_out[12], 1'b1, 1'b1, BUS_in[5], dip_7404_1_p4, Bus_out[13]
  // DIP_7408 AND_5: pin names not known; wires that end beside it: Bus_out[5], Bus_out[2], XOR_p8[5], XOR_p8[2], XOR_p8[6], XOR_p8[3], Bus_out[4], Bus_out[3], XOR_p8[4], XOR_p8[3], XOR_p8[5], XOR_p8[4]
  // DIP_7474 D_FF_6: pin names not known; wires that end beside it: 1'b1, D_FF_2_p2[4], dip_7404_1_p6, 1'b1, Bus_out[4], 1'b1, 1'b1, D_FF_2_p2[5], dip_7404_1_p6, Bus_out[5]
  // DIP_7474 D_FF_7: pin names not known; wires that end beside it: 1'b1, D_FF_2_p2[6], dip_7404_1_p6, 1'b1, Bus_out[6], 1'b1, 1'b1, D_FF_2_p2[7], dip_7404_1_p6, Bus_out[7]
  // DIP_7474 D_FF_8: pin names not known; wires that end beside it: 1'b1, BUS_in[6], dip_7404_1_p4, 1'b1, Bus_out[14], 1'b1, 1'b1, BUS_in[7], dip_7404_1_p4, Bus_out[15]
  // DIP_74157 MUX: pin names not known; wires that end beside it: Clock, AND_2_p3[0], XOR_p6[0], MUX_p4[0], AND_2_p3[1], 1'b0, AND_2_p3[7], XOR_p6[7], MUX_p4[7]
  // DIP_74157 MUX_2: pin names not known; wires that end beside it: XOR_p6[1], MUX_p4[1], Clock, AND_2_p3[2], XOR_p6[2], MUX_p4[2], AND_2_p3[3], XOR_p6[3], MUX_p4[3], AND_2_p3[6], XOR_p6[6], MUX_p4[6], 1'b0, AND_2_p3[5], XOR_p6[5], MUX_p4[5], AND_2_p3[4], XOR_p6[4], MUX_p4[4]
  assign buffer_1_out = MUX_p4;  // Buffer buffer_1, 8 bits wide
  assign buffer_2_out = buffer_1_out;  // Buffer buffer_2, 8 bits wide
  assign D_FF_2_p2 = buffer_2_out;  // Buffer buffer_3, 8 bits wide
endmodule

module ALU74 (
  input  [7:0] A,
  input  [7:0] B,
  input  [3:0] CU,
  output Garry,
  output Zero,
  output [7:0] Bus
);

  wire ADD_carry, CMPZERO_is_zero;
  wire [7:0] ADD_summe, AND_out_3, mux_1_output_accu, OR_out_3, SHL_output_acc, SHR_output_acc, XOR_out_3;

  ADD74 ADD (.SUB_A(CU[1]), .B(B), .SUMME(ADD_summe), .CARRY(ADD_carry), .A(A), .SUB_B(CU[0]));
  AND74 AND (.A(A), .B(B), .out_3(AND_out_3));
  OR74 OR (.A(A), .B(B), .out_3(OR_out_3));
  XOR74 XOR (.A(A), .B(B), .out_3(XOR_out_3));
  SHL74 SHL (.B(B), .A(A), .Output_Acc(SHL_output_acc));
  SHR74 SHR (.B(B), .A(A), .Output_Acc(SHR_output_acc));
  MUX mux_1 (
    .ADD(ADD_summe), .SUB(ADD_summe), .AND(AND_out_3), .OR(OR_out_3), .XOR(XOR_out_3), .SHL(SHL_output_acc),
    .SHR(SHR_output_acc), .A(A), .Output_Accu(mux_1_output_accu), .CU(CU[2:0]));
  // Probe on SHR_output_acc
  // Probe on SHL_output_acc
  // Probe on XOR_out_3
  // Probe on OR_out_3
  // Probe on AND_out_3
  // Probe on ADD_summe
  CMPZERO74 CMPZERO (.Input(mux_1_output_accu), .is_zero(CMPZERO_is_zero));
  // DIP_7486 XOR_3: pin names not known; wires that end beside it: CMPZERO_is_zero, CU[3], CU[3], ADD_carry, Zero, Garry
  INV74 INV (.Input(mux_1_output_accu), .Output(Bus), .INV(CU[3]));
  // Probe on mux_1_output_accu
endmodule

module ControlUnit74 (
  input  Clock,
  input  Reset,
  input  [7:0] Bus_in,
  input  [7:0] in_4,
  input  Carry,
  input  isZero,
  output Increment_P,
  output [2:0] Bus_Input,
  output [2:0] Update_Reg,
  output Reset_P1,
  output [3:0] Alu,
  output Update_RAMSOSSE,
  output RAM_select_M,
  output [1:0] Update_IR
);

  wire AND_2_p3, AND_2_p4, AND_2_p5, AND_2_p6, AND_p1, AND_p2, AND_p3, buffer_2_out, buffer_3_out,
       buffer_4_out, buffer_5_out, buffer_6_out, buffer_7_out, buffer_8_out, buffer_9_out, buffer_10_out,
       buffer_11_out, buffer_12_out, buffer_13_out, buffer_14_out, buffer_15_out, buffer_17_out,
       buffer_18_out, mux_p1, mux_p6, mux_p8;
  wire [1:0] INCR_p5;
  wire [7:0] D_2_p14;

  // DIP_7408 AND: pin names not known; wires that end beside it: AND_p1, AND_p2, AND_p3
  // DIP_7474 INCR: pin names not known; wires that end beside it: 1'b1, AND_p1, Clock, 1'b1, INCR_p5[0], AND_p1, 1'b1, 1'b1, AND_p2, AND_p1, INCR_p5[1], AND_p2
  // DIP_74157 D: pin names not known; wires that end beside it: Reset, Bus_in[6], 1'b1, D_2_p14[6], Bus_in[7], 1'b1, D_2_p14[7], 1'b0, Bus_in[5], 1'b1, D_2_p14[5], Bus_in[4], 1'b1, D_2_p14[4]
  // DIP_74153 mux: pin names not known; wires that end beside it: mux_p1, AND_p3, AND_p3, Carry, isZero, mux_p6, 1'b1, mux_p8, 1'b1
  // DIP_7408 AND_2: pin names not known; wires that end beside it: mux_p1, Clock, AND_2_p3, AND_2_p4, AND_2_p5, AND_2_p6
  // DIP_74157 D_2: pin names not known; wires that end beside it: Reset, Bus_in[2], 1'b1, D_2_p14[2], Bus_in[3], 1'b1, D_2_p14[3], 1'b0, Bus_in[1], 1'b1, D_2_p14[1], Bus_in[0], 1'b1, D_2_p14[0]
  REGISTER74 IR (.Input(D_2_p14), .Set(AND_2_p3), .Output(in_4));
  // DIP_7474 High_Low: pin names not known; wires that end beside it: 1'b1, 1'b1, Update_IR[0], 1'b1, Clock, Update_IR[1], 1'b1, Clock, mux_p6, mux_p8
  buf buffer_1 (AND_2_p5, buffer_3_out);
  buf buffer_2 (buffer_2_out, buffer_9_out);
  buf buffer_3 (buffer_3_out, buffer_2_out);
  buf buffer_4 (buffer_4_out, Clock);
  buf buffer_5 (buffer_5_out, buffer_4_out);
  buf buffer_6 (buffer_6_out, buffer_8_out);
  buf buffer_7 (buffer_7_out, buffer_14_out);
  buf buffer_8 (buffer_8_out, buffer_7_out);
  buf buffer_9 (buffer_9_out, buffer_6_out);
  buf buffer_10 (buffer_10_out, buffer_11_out);
  buf buffer_11 (buffer_11_out, buffer_13_out);
  buf buffer_12 (buffer_12_out, buffer_5_out);
  buf buffer_13 (buffer_13_out, buffer_12_out);
  buf buffer_14 (buffer_14_out, buffer_15_out);
  buf buffer_15 (buffer_15_out, AND_2_p4);
  buf buffer_16 (AND_2_p4, buffer_17_out);
  buf buffer_17 (buffer_17_out, buffer_18_out);
  buf buffer_18 (buffer_18_out, buffer_10_out);
  ROM #(.addrWidth(10), .dataWidth(16)) rom_1 (
    .addr({in_4, INCR_p5}),
    .data({Update_IR[0], Update_IR[1], RAM_select_M, Update_RAMSOSSE, Alu, Reset_P1, Update_Reg, Bus_Input, Increment_P}),
    .sel(AND_2_p6));
  Pull_Resistor pull_resistor_1 (.node({Update_IR[0], Update_IR[1], RAM_select_M, Update_RAMSOSSE, Alu, Reset_P1, Update_Reg, Bus_Input, Increment_P}));

  // Notes on the sheet:
  //   contents of rom_1 (hex, n*v repeats v):
  //   0 0 0 1 0 0 4002 1 0 0 4012 1 0 0 4022 1 0 0 4032 1 0 0 3002 1 0 0 4042 1 0 0 4052 1 0 0 4102 1 0 0
  //   4112 1 0 0 4122 1 0 0 4132 1 0 0 3102 1 0 0 4142 1 0 0 4152 1 0 0 4202 1 0 0 4212 1 0 0 4222 1 0 0
  //   4232 1 0 0 3202 1 0 0 4242 1 0 0 4252 1 0 0 4302 1 0 0 4312 1 0 0 4322 1 0 0 4332 1 0 0 3302 1 0 0
  //   4342 1 0 0 4352 1 0 0 4402 1 0 0 4412 1 0 0 4422 1 0 0 4432 1 0 0 3402 1 0 0 4442 1 0 0 4452 1 0 0
  //   4f02 1 0 0 4f12 1 0 0 4f22 1 0 0 4f32 1 0 0 3f02 1 0 0 4f42 1 0 0 4f52 1 0 0 4602 1 0 0 4612 1 0 0
  //   4622 1 0 0 4632 1 0 0 3602 1 0 0 4642 1 0 0 4652 1 0 0 4502 1 0 0 4512 1 0 0 4522 1 0 0 4532 1 0 0
  //   3502 1 0 0 4542 1 0 0 4552 1 0 0 4018 1 0 0 4028 1 0 0 4038 1 0 0 3008 1 0 0 4048 1 0 0 4058 1 0 0
  //   400a 1 0 0 402a 1 0 0 403a 1 0 0 300a 1 0 0 404a 1 0 0 405a 1 0 0 400c 1 0 0 401c 1 0 0 403c 1 0 0
  //   300c 1 0 0 404c 1 0 0 405c 1 0 0 400e 1 0 0 401e 1 0 0 402e 1 0 0 300e 1 0 0 404e 1 0 0 405e 1 0 0
  //   6000 1 0 0 6010 1 0 0 6020 1 0 0 6030 1 0 0 6040 1 0 0 6050 1 0 1 4000 1 0 1 4010 1 0 1 4020 1 0 1
  //   4030 1 0 1 4040 1 0 1 4050 1 0 4402 4412 4403 11*0 4068 0 0 0 406a 0 0 0 406c 0 0 0 406e 0 0 0 6060
  //   0 0 1 4060 0 0 0 40f8 0 0 0 40fa 0 0 0 40fc 0 0 0 40fe 0 0 0 60f0 0 0 1 40f0 0 0 4078 406a 0 0 4078
  //   406c 0 0 4078 406e 0 0 4078 6060 0 1 4060 4078 0 0 407a 4068 0 0 407a 406c 0 0 407a 406e 0 0 407a
  //   6060 0 1 4060 407a 0 0 407c 4068 0 0 407c 406a 0 0 407c 406e 0 0 407c 6060 0 1 4060 407c 0 0 407e
  //   4068 0 0 407e 406a 0 0 407e 406c 0 0 407e 6060 0 1 4060 407e 0 0 6070 4068 0 0 6070 406a 0 0 6070
  //   406c 0 0 6070 406e 0 1 4060 6070 0 1 4070 4068 0 1 4070 406a 0 1 4070 406c 0 1 4070 406e 0 1 4070
  //   6060 216*0 c701 1 0 0 cf01 1 0 0 8201 1 0 0 8901 1 0 0 c101 1 0 0 c901 1 0 0 8a01 1 0 0 8101 1 0 0
  //   c701 1 1 0 cf01 1 1 0 8201 1 1 0 8901 1 1 0 c101 1 1 0 c901 1 1 0 8a01 1 1 0 8101 1 1
endmodule

// Reg
module REGISTER74 (
  input  [7:0] Input,
  input  Set,
  output [7:0] Output
);

  wire dip_7404_1_p2;

  // DIP_7404 dip_7404_1: pin names not known; wires that end beside it: Set, dip_7404_1_p2
  // DIP_7474 dip_7474_1: pin names not known; wires that end beside it: 1'b1, Input[7], dip_7404_1_p2, 1'b1, Output[7], 1'b1, 1'b1, Input[0], dip_7404_1_p2
  // DIP_7474 dip_7474_2: pin names not known; wires that end beside it: 1'b1, Input[6], dip_7404_1_p2, 1'b1, Output[6], Output[0], 1'b1, 1'b1, Input[1], dip_7404_1_p2
  // DIP_7474 dip_7474_3: pin names not known; wires that end beside it: 1'b1, Input[5], dip_7404_1_p2, 1'b1, Output[5], Output[1], 1'b1, 1'b1, Input[2], dip_7404_1_p2
  // DIP_7474 dip_7474_4: pin names not known; wires that end beside it: 1'b1, Input[4], dip_7404_1_p2, 1'b1, Output[4], Output[2], 1'b1, 1'b1, Input[3], dip_7404_1_p2, Output[3]
endmodule

module AND74 (
  input  [7:0] A,
  input  [7:0] B,
  output [7:0] out_3
);

  // DIP_7408 AND: pin names not known; wires that end beside it: B[7], B[3], A[7], A[3], out_3[7], out_3[3], B[6], B[2], A[6]
  // DIP_7408 AND_2: pin names not known; wires that end beside it: A[2], out_3[6], out_3[2], B[5], B[1], A[5], A[1], out_3[5], out_3[1], B[4], B[0], A[4], A[0], out_3[4], out_3[0]
endmodule

module OR74 (
  input  [7:0] A,
  input  [7:0] B,
  output [7:0] out_3
);

  // DIP_7432 OR: pin names not known; wires that end beside it: B[7], B[3], A[7], A[3], out_3[7], out_3[3], B[6], B[2], A[6]
  // DIP_7432 OR_2: pin names not known; wires that end beside it: A[2], out_3[6], out_3[2], B[5], B[1], A[5], A[1], out_3[5], out_3[1], B[4], B[0], A[4], A[0], out_3[4], out_3[0]
endmodule

module XOR74 (
  input  [7:0] A,
  input  [7:0] B,
  output [7:0] out_3
);

  // DIP_7486 XOR: pin names not known; wires that end beside it: B[7], B[3], A[7], A[3], out_3[7], out_3[3], B[6], B[2], A[6]
  // DIP_7486 XOR_2: pin names not known; wires that end beside it: A[2], out_3[6], out_3[2], B[5], B[1], A[5], A[1], out_3[5], out_3[1], B[4], B[0], A[4], A[0], out_3[4], out_3[0]
endmodule

module ADD74 (
  input  SUB_A,
  input  SUB_B,
  input  [7:0] A,
  input  [7:0] B,
  output [7:0] SUMME,
  output CARRY
);

  wire OR_p5, XOR_9_p7;
  wire [7:0] AND_4_p14, AND_4_p15, XOR_4_p15, XOR_6_p14, XOR_8_p11, XOR_p5;

  // DIP_7486 XOR: pin names not known; wires that end beside it: A[0], SUB_B, SUB_A, B[7], XOR_p5[0], XOR_4_p15[7], A[1], SUB_B, SUB_A
  // DIP_7486 XOR_2: pin names not known; wires that end beside it: B[6], XOR_p5[1], XOR_4_p15[6], A[2], SUB_B, SUB_A, B[5], XOR_p5[2], XOR_4_p15[5], A[3], SUB_B, SUB_A
  // DIP_7486 XOR_3: pin names not known; wires that end beside it: B[4], XOR_p5[3], XOR_4_p15[4], A[4], SUB_B, SUB_A, B[3], XOR_p5[4], XOR_4_p15[3], A[5], SUB_B, SUB_A
  // DIP_7486 XOR_4: pin names not known; wires that end beside it: B[2], XOR_p5[5], XOR_4_p15[2], A[6], SUB_B, SUB_A, B[1], XOR_p5[6], XOR_4_p15[1], SUB_A, SUB_B, A[7], B[0], XOR_p5[7], XOR_4_p15[0]
  // DIP_7486 XOR_5: pin names not known; wires that end beside it: XOR_p5[3], XOR_p5[4], XOR_4_p15[3], XOR_4_p15[4], XOR_6_p14[3], XOR_6_p14[4], XOR_p5[2], XOR_p5[5], XOR_4_p15[2]
  // DIP_7486 XOR_6: pin names not known; wires that end beside it: XOR_4_p15[5], XOR_6_p14[2], XOR_6_p14[5], XOR_p5[1], XOR_p5[6], XOR_4_p15[1], XOR_4_p15[6], XOR_6_p14[1], XOR_6_p14[6], XOR_p5[0], XOR_p5[7], XOR_4_p15[0], XOR_4_p15[7], XOR_6_p14[0], XOR_6_p14[7]
  // DIP_7408 AND: pin names not known; wires that end beside it: XOR_8_p11[7], XOR_p5[7], XOR_6_p14[7], XOR_4_p15[7], AND_4_p14[7], AND_4_p15[7], XOR_8_p11[6], XOR_p5[6], XOR_6_p14[6]
  // DIP_7408 AND_2: pin names not known; wires that end beside it: XOR_4_p15[6], AND_4_p14[6], AND_4_p15[6], XOR_8_p11[5], XOR_p5[5], XOR_6_p14[5], XOR_4_p15[5], AND_4_p14[5], AND_4_p15[5], XOR_8_p11[4], XOR_p5[4], XOR_6_p14[4]
  // DIP_7408 AND_3: pin names not known; wires that end beside it: XOR_4_p15[4], AND_4_p14[4], AND_4_p15[4], XOR_8_p11[3], XOR_p5[3], XOR_6_p14[3], XOR_4_p15[3], AND_4_p14[3], AND_4_p15[3], XOR_8_p11[2], XOR_p5[2], XOR_6_p14[2]
  // DIP_7486 XOR_7: pin names not known; wires that end beside it: XOR_8_p11[7], XOR_8_p11[3], XOR_6_p14[7], XOR_6_p14[3], SUMME[7], SUMME[3], XOR_8_p11[6], XOR_8_p11[2], XOR_6_p14[6]
  // DIP_7486 XOR_8: pin names not known; wires that end beside it: XOR_6_p14[2], SUMME[6], SUMME[2], XOR_8_p11[5], XOR_8_p11[1], XOR_6_p14[5], XOR_6_p14[1], SUMME[5], SUMME[1], XOR_8_p11[4], XOR_8_p11[0], XOR_6_p14[4], XOR_6_p14[0], SUMME[4], SUMME[0]
  // DIP_7408 AND_4: pin names not known; wires that end beside it: XOR_4_p15[2], AND_4_p14[2], AND_4_p15[2], XOR_8_p11[1], XOR_p5[1], XOR_6_p14[1], XOR_4_p15[1], AND_4_p14[1], AND_4_p15[1], XOR_8_p11[0], XOR_p5[0], XOR_6_p14[0], XOR_4_p15[0], AND_4_p14[0], AND_4_p15[0]
  // DIP_7432 OR: pin names not known; wires that end beside it: AND_4_p14[7], AND_4_p14[3], AND_4_p15[7], AND_4_p15[3], OR_p5, XOR_8_p11[4], AND_4_p14[6], AND_4_p14[2], AND_4_p15[6]
  // DIP_7486 XOR_9: pin names not known; wires that end beside it: SUB_B, SUB_A, XOR_8_p11[0], SUB_B, OR_p5, SUB_A, XOR_9_p7, XOR_9_p7, CARRY
  // DIP_7432 OR_2: pin names not known; wires that end beside it: AND_4_p15[2], XOR_8_p11[7], XOR_8_p11[3], AND_4_p14[5], AND_4_p14[1], AND_4_p15[5], AND_4_p15[1], XOR_8_p11[6], XOR_8_p11[2], AND_4_p14[4], AND_4_p14[0], AND_4_p15[4], AND_4_p15[0], XOR_8_p11[5], XOR_8_p11[1]

  // Notes on the sheet:
  //   CARRY
endmodule

module SHL74 (
  input  [7:0] A,
  input  [7:0] B,
  output [7:0] Output_Acc
);

  wire AND_2_p6, AND_2_p7, AND_2_p12, AND_2_p13, AND_p3, AND_p9, MUX_8_in_2_p5, MUX_8_in_p5, NOT_p3, OR_p3,
       OR_p4, OR_p5, OR_p6;

  // DIP_7432 OR: pin names not known; wires that end beside it: B[7], B[5], OR_p3, OR_p4, OR_p5, OR_p6, B[6], B[4], OR_p6, B[3], OR_p4
  // DIP_7404 NOT: pin names not known; wires that end beside it: OR_p3, OR_p5, NOT_p3
  // DIP_74151 MUX_8_in: pin names not known; wires that end beside it: 1'b0, 1'b0, 1'b0, A[0], MUX_8_in_p5, 1'b0, 1'b0, 1'b0, 1'b0, 1'b0, B[0], B[1], B[2]
  // DIP_7408 AND: pin names not known; wires that end beside it: NOT_p3, NOT_p3, AND_p3, MUX_8_in_p5, Output_Acc[4], Output_Acc[0], NOT_p3, NOT_p3, AND_p9
  // DIP_74151 MUX_8_in_2: pin names not known; wires that end beside it: 1'b0, 1'b0, A[0], A[1], MUX_8_in_2_p5, 1'b0, 1'b0, 1'b0, 1'b0, 1'b0, B[0], B[1], B[2]
  // DIP_7408 AND_2: pin names not known; wires that end beside it: MUX_8_in_2_p5, Output_Acc[5], Output_Acc[1], NOT_p3, NOT_p3, AND_2_p6, AND_2_p7, Output_Acc[6], Output_Acc[2], NOT_p3, NOT_p3, AND_2_p12, AND_2_p13, Output_Acc[7], Output_Acc[3]
  // DIP_74151 MUX_8_in_3: pin names not known; wires that end beside it: 1'b0, A[0], A[1], A[2], AND_2_p7, 1'b0, 1'b0, 1'b0, 1'b0, 1'b0, B[0], B[1], B[2]
  // DIP_74151 MUX_8_in_4: pin names not known; wires that end beside it: A[0], A[1], A[2], A[3], AND_2_p13, 1'b0, 1'b0, 1'b0, 1'b0, 1'b0, B[0], B[1], B[2]
  // DIP_74151 MUX_8_in_5: pin names not known; wires that end beside it: A[1], A[2], A[3], A[4], AND_p3, 1'b0, A[0], 1'b0, 1'b0, 1'b0, B[0], B[1], B[2]
  // DIP_74151 MUX_8_in_6: pin names not known; wires that end beside it: A[2], A[3], A[4], A[5], AND_p9, 1'b0, A[1], A[0], 1'b0, 1'b0, B[0], B[1], B[2]
  // DIP_74151 MUX_8_in_7: pin names not known; wires that end beside it: A[3], A[4], A[5], A[6], AND_2_p6, 1'b0, A[2], A[1], A[0], 1'b0, B[0], B[1], B[2]
  // DIP_74151 MUX_8_in_8: pin names not known; wires that end beside it: A[4], A[5], A[6], A[7], AND_2_p12, 1'b0, A[3], A[2], A[1], A[0], B[0], B[1], B[2]
endmodule

module SHR74 (
  input  [7:0] A,
  input  [7:0] B,
  output [7:0] Output_Acc
);

  wire AND_2_p6, AND_2_p7, AND_2_p12, AND_2_p13, AND_p3, AND_p9, MUX_8_in_2_p5, MUX_8_in_p5, NOT_p3, OR_p3,
       OR_p4, OR_p5, OR_p6;

  // DIP_7432 OR: pin names not known; wires that end beside it: B[7], B[5], OR_p3, OR_p4, OR_p5, OR_p6, B[6], B[4], OR_p6, B[3], OR_p4
  // DIP_7404 NOT: pin names not known; wires that end beside it: OR_p3, OR_p5, NOT_p3
  // DIP_74151 MUX_8_in: pin names not known; wires that end beside it: 1'b0, 1'b0, 1'b0, A[7], MUX_8_in_p5, 1'b0, 1'b0, 1'b0, 1'b0, 1'b0, B[0], B[1], B[2]
  // DIP_7408 AND: pin names not known; wires that end beside it: NOT_p3, NOT_p3, AND_p3, MUX_8_in_p5, Output_Acc[3], Output_Acc[7], NOT_p3, NOT_p3, AND_p9
  // DIP_74151 MUX_8_in_2: pin names not known; wires that end beside it: 1'b0, 1'b0, A[7], A[6], MUX_8_in_2_p5, 1'b0, 1'b0, 1'b0, 1'b0, 1'b0, B[0], B[1], B[2]
  // DIP_7408 AND_2: pin names not known; wires that end beside it: MUX_8_in_2_p5, Output_Acc[2], Output_Acc[6], NOT_p3, NOT_p3, AND_2_p6, AND_2_p7, Output_Acc[1], Output_Acc[5], NOT_p3, NOT_p3, AND_2_p12, AND_2_p13, Output_Acc[0], Output_Acc[4]
  // DIP_74151 MUX_8_in_3: pin names not known; wires that end beside it: 1'b0, A[7], A[6], A[5], AND_2_p7, 1'b0, 1'b0, 1'b0, 1'b0, 1'b0, B[0], B[1], B[2]
  // DIP_74151 MUX_8_in_4: pin names not known; wires that end beside it: A[7], A[6], A[5], A[4], AND_2_p13, 1'b0, 1'b0, 1'b0, 1'b0, 1'b0, B[0], B[1], B[2]
  // DIP_74151 MUX_8_in_5: pin names not known; wires that end beside it: A[6], A[5], A[4], A[3], AND_p3, 1'b0, A[7], 1'b0, 1'b0, 1'b0, B[0], B[1], B[2]
  // DIP_74151 MUX_8_in_6: pin names not known; wires that end beside it: A[5], A[4], A[3], A[2], AND_p9, 1'b0, A[6], A[7], 1'b0, 1'b0, B[0], B[1], B[2]
  // DIP_74151 MUX_8_in_7: pin names not known; wires that end beside it: A[4], A[3], A[2], A[1], AND_2_p6, 1'b0, A[5], A[6], A[7], 1'b0, B[0], B[1], B[2]
  // DIP_74151 MUX_8_in_8: pin names not known; wires that end beside it: A[3], A[2], A[1], A[0], AND_2_p12, 1'b0, A[4], A[5], A[6], A[7], B[0], B[1], B[2]
endmodule

module INV74 (
  input  [7:0] Input,
  input  INV,
  output [7:0] Output
);

  wire [7:0] bit_extender_1_out;

  assign bit_extender_1_out = {{7{INV}}, INV};  // Bit_Extender bit_extender_1
  // DIP_7486 XOR: pin names not known; wires that end beside it: bit_extender_1_out[7], bit_extender_1_out[4], Input[7], Input[3], Output[7], Output[3], bit_extender_1_out[6], bit_extender_1_out[5], Input[6], Input[2], Output[6], Output[2]
  // DIP_7486 XOR_2: pin names not known; wires that end beside it: bit_extender_1_out[1], bit_extender_1_out[2], Input[5], Input[1], Output[5], Output[1], bit_extender_1_out[0], bit_extender_1_out[3], Input[4], Input[0], Output[4], Output[0]
endmodule

module CMPZERO74 (
  input  [7:0] Input,
  output is_zero
);

  wire OR_2_p5, OR_2_p6, OR_p3, OR_p4, OR_p5, OR_p10, OR_p11;

  // DIP_7432 OR: pin names not known; wires that end beside it: Input[5], Input[4], OR_p3, OR_p4, OR_p5, OR_p3, OR_p5, Input[3], Input[6], OR_p10, OR_p11
  // DIP_7432 OR_2: pin names not known; wires that end beside it: OR_p4, OR_p11, Input[2], Input[7], OR_2_p5, OR_2_p6, OR_p10, Input[1]
  // DIP_7404 NOT: pin names not known; wires that end beside it: Input[0], OR_2_p5, OR_2_p6, is_zero
endmodule

module MUX (
  input  [7:0] ADD,
  input  [2:0] CU,
  input  [7:0] SUB,
  input  [7:0] AND,
  input  [7:0] OR,
  input  [7:0] XOR,
  input  [7:0] SHL,
  input  [7:0] SHR,
  input  [7:0] A,
  output [7:0] Output_Accu
);

  Mux2bit MUX_Modul (
    ._8_Bit_input_1({A[0], SHR[0], SHL[0], XOR[0], OR[0], AND[0], SUB[0], ADD[0]}), .Bit_2(Output_Accu[1]),
    .Bit_1(Output_Accu[0]), .CU(CU),
    ._8_Bit_input_1_2({A[1], SHR[1], SHL[1], XOR[1], OR[1], AND[1], SUB[1], ADD[1]}));
  Mux2bit MUX_Modul_2 (
    ._8_Bit_input_1({A[2], SHR[2], SHL[2], XOR[2], OR[2], AND[2], SUB[2], ADD[2]}), .Bit_2(Output_Accu[3]),
    .Bit_1(Output_Accu[2]), .CU(CU),
    ._8_Bit_input_1_2({A[3], SHR[3], SHL[3], XOR[3], OR[3], AND[3], SUB[3], ADD[3]}));
  Mux2bit MUX_Modul_3 (
    ._8_Bit_input_1({A[4], SHR[4], SHL[4], XOR[4], OR[4], AND[4], SUB[4], ADD[4]}), .Bit_2(Output_Accu[5]),
    .Bit_1(Output_Accu[4]), .CU(CU),
    ._8_Bit_input_1_2({A[5], SHR[5], SHL[5], XOR[5], OR[5], AND[5], SUB[5], ADD[5]}));
  Mux2bit MUX_Modul_4 (
    ._8_Bit_input_1({A[6], SHR[6], SHL[6], XOR[6], OR[6], AND[6], SUB[6], ADD[6]}), .Bit_2(Output_Accu[7]),
    .Bit_1(Output_Accu[6]), .CU(CU),
    ._8_Bit_input_1_2({A[7], SHR[7], SHL[7], XOR[7], OR[7], AND[7], SUB[7], ADD[7]}));
endmodule

module Mux2bit (
  input  [2:0] CU,
  input  [7:0] _8_Bit_input_1,
  input  [7:0] _8_Bit_input_1_2,
  output Bit_1,
  output Bit_2
);

  // DIP_74151 dip_74151_1: pin names not known; wires that end beside it: _8_Bit_input_1[3], _8_Bit_input_1[2], _8_Bit_input_1[1], _8_Bit_input_1[0], Bit_1, 1'b0, _8_Bit_input_1[4], _8_Bit_input_1[5], _8_Bit_input_1[6], _8_Bit_input_1[7], CU[0], CU[1], CU[2]
  // DIP_74151 dip_74151_2: pin names not known; wires that end beside it: _8_Bit_input_1_2[3], _8_Bit_input_1_2[2], _8_Bit_input_1_2[1], _8_Bit_input_1_2[0], Bit_2, 1'b0, _8_Bit_input_1_2[4], _8_Bit_input_1_2[5], _8_Bit_input_1_2[6], _8_Bit_input_1_2[7], CU[0], CU[1], CU[2]
endmodule

module test (
  input  in_1,
  input  in_2,
  input  in_3,
  input  in_4
);

  wire dip_74157_1_p4;

  // DIP_74157 dip_74157_1: pin names not known; wires that end beside it: in_2, in_4, in_3, dip_74157_1_p4, in_1
endmodule
